# Fritzing sketch Arduino_calculator (saved by Fritzing 0.9.3b)
breadboards: 1

parts:
  Keypad4x1 = Keypad Membran 4x4
  부품1 = Arduino Mega 2560 (Rev3)
  7_Segment_4_Digit_Display1 = 7-SEGMENT-4DIGIT common anode [part_number="5461BS - 5462BS" package=7-segment-4digit-anode]
  7_Segment_4_Digit_Display2 = 7-SEGMENT-4DIGIT common anode [part_number="5461BS - 5462BS" package=7-segment-4digit-anode]
  R1 = Resistor [tolerance=±5% resistance=220 package=THT]
  R2 = Resistor [tolerance=±5% resistance=220 package=THT]
  R3 = Resistor [tolerance=±5% resistance=220 package=THT]
  R4 = Resistor [tolerance=±5% resistance=220 package=THT]
  R5 = Resistor [tolerance=±5% resistance=220 package=THT]
  R6 = Resistor [tolerance=±5% resistance=220 package=THT]
  R7 = Resistor [tolerance=±5% resistance=220 package=THT]
  R8 = Resistor [tolerance=±5% resistance=220 package=THT]

nets:
  N1: Keypad4x1.Pin1, 부품1.D29
  N2: Keypad4x1.Pin2, 부품1.D28
  N3: Keypad4x1.Pin3, 부품1.D27
  N4: Keypad4x1.Pin4, 부품1.D26
  N5: Keypad4x1.Pin5, 부품1.D25
  N6: Keypad4x1.Pin6, 부품1.D24
  N7: Keypad4x1.Pin7, 부품1.D23
  N8: Keypad4x1.Pin8, 부품1.D22
  N9: 부품1.D13_PWM, R5.Pin_1
  N10: 부품1.D12_PWM, R6.Pin_1
  N11: 부품1.D11_PWM, R7.Pin_1
  N12: 부품1.D10_PWM, R8.Pin_1
  N13: 부품1.D9_PWM, 7_Segment_4_Digit_Display2.pin_11
  N14: 부품1.D8_PWM, 7_Segment_4_Digit_Display2.pin_10
  N15: 부품1.D2_PWM, 7_Segment_4_Digit_Display2.pin_7
  N16: 부품1.D3_PWM, 7_Segment_4_Digit_Display2.pin_4
  N17: 부품1.D4_PWM, 7_Segment_4_Digit_Display2.pin_3
  N18: 부품1.D5_PWM, 7_Segment_4_Digit_Display2.pin_2
  N19: 부품1.D6_PWM, 7_Segment_4_Digit_Display2.pin_1
  N20: 부품1.D7_PWM, 7_Segment_4_Digit_Display2.pin_5
  N21: 부품1.D32, 7_Segment_4_Digit_Display1.pin_7
  N22: 부품1.D33, 7_Segment_4_Digit_Display1.pin_4
  N23: 부품1.D34, 7_Segment_4_Digit_Display1.pin_3
  N24: 부품1.D35, 7_Segment_4_Digit_Display1.pin_2
  N25: 부품1.D36, 7_Segment_4_Digit_Display1.pin_1
  N26: 부품1.D37, 7_Segment_4_Digit_Display1.pin_5
  N27: 부품1.D38, 7_Segment_4_Digit_Display1.pin_10
  N28: 부품1.D39, 7_Segment_4_Digit_Display1.pin_11
  N29: 부품1.D40, R4.Pin_1
  N30: 부품1.D41, R3.Pin_1
  N31: 부품1.D42, R2.Pin_1
  N32: 부품1.D43, R1.Pin_1
  N33: 7_Segment_4_Digit_Display1.pin_6, R1.Pin_0
  N34: 7_Segment_4_Digit_Display1.pin_8, R2.Pin_0
  N35: 7_Segment_4_Digit_Display1.pin_9, R3.Pin_0
  N36: 7_Segment_4_Digit_Display1.pin_12, R4.Pin_0
  N37: 7_Segment_4_Digit_Display2.pin_6, R5.Pin_0
  N38: 7_Segment_4_Digit_Display2.pin_8, R6.Pin_0
  N39: 7_Segment_4_Digit_Display2.pin_9, R7.Pin_0
  N40: 7_Segment_4_Digit_Display2.pin_12, R8.Pin_0

custom parts:
  Keypad Membran 4x4: Membrane Keypad 4x4 Matrix
  7-SEGMENT-4DIGIT common anode: A 7 Segment 4 Digit common anode display, with decimal points
